# Fritzing sketch Tetris (saved by Fritzing 0.9.3b)
breadboards: 1

parts:
  Banggood_Display1 = Banggood Display
  LPC1114ETF1 = LPC1114ETF razvojni sistem
  Part1 = ETF Joystick

nets:
  N1: Banggood_Display1.RST, LPC1114ETF1.dp23
  N2: Banggood_Display1.CS, LPC1114ETF1.dp24
  N3: Banggood_Display1.DC, LPC1114ETF1.dp25
  N4: Banggood_Display1.SDI, LPC1114ETF1.dp2
  N5: Banggood_Display1.SCK, LPC1114ETF1.dp6
  VCC: Banggood_Display1.VCC, Banggood_Display1.LED, LPC1114ETF1.+3.3V, Part1.+5V
  N6: Banggood_Display1.GND, LPC1114ETF1.GND#22
  N7: Banggood_Display1.SDO, LPC1114ETF1.dp1
  N8: LPC1114ETF1.dp9, Part1.SW
  N9: LPC1114ETF1.dp10, Part1.VRy
  N10: LPC1114ETF1.dp11, Part1.VRx
  N11: LPC1114ETF1.GND#21, Part1.GND
